# Fritzing sketch schematic (saved by Fritzing 0.9.2b)
breadboards: 1

parts:
  Bauteil1 = Arduino Nano (Rev3.0)
  NEOPIXEL1 = Neopixel Strip -- White (60/m)
  NEOPIXEL2 = Neopixel Strip -- White (60/m)
  NEOPIXEL3 = Neopixel Strip -- White (60/m)
  NEOPIXEL4 = Neopixel Strip -- White (60/m)
  NEOPIXEL5 = Neopixel Strip -- White (60/m)
  NEOPIXEL6 = Neopixel Strip -- White (60/m)
  NEOPIXEL7 = Neopixel Strip -- White (60/m)
  IC1 = MSGEQ7 [package=soic8]
  R1 = Resistor [tolerance=±5% resistance=220 package=THT]
  R2 = Resistor [tolerance=±5% resistance=220 package=THT]
  R3 = Resistor [tolerance=±5% resistance=220 package=THT]
  R4 = Resistor [tolerance=±5% resistance=220 package=THT]
  R5 = Resistor [tolerance=±5% resistance=220 package=THT]
  R6 = Resistor [tolerance=±5% resistance=220 package=THT]
  R7 = Resistor [tolerance=±5% resistance=220 package=THT]
  U1 = 3.5mm Audio Jack [package=audio-jack-3.5mm-smd]
  R8 = Resistor [tolerance=±5% resistance=22k package=THT]
  R9 = Resistor [tolerance=±5% resistance=22k package=THT]
  C1 = Ceramic Capacitor [capacitance=10nF package="100 mil [THT, multilayer]"]
  R10 = Resistor [tolerance=±5% resistance=200k package=THT]
  C2 = Ceramic Capacitor [capacitance=33pF package="100 mil [THT, multilayer]"]
  C3 = Ceramic Capacitor [capacitance=100nF package="100 mil [THT, multilayer]"]
  C4 = Ceramic Capacitor [capacitance=100nF package="100 mil [THT, multilayer]"]

nets (from the breadboard view):
  GND: Bauteil1.GND, NEOPIXEL7.GND#3, IC1.GND, IC1.RESET, C2.0, C3.0, C4.1
  N1: Bauteil1.D2, R1.Pin_1
  N2: Bauteil1.D3, R7.Pin_1
  N3: Bauteil1.D4, R6.Pin_1
  N4: Bauteil1.D5, R5.Pin_1
  N5: Bauteil1.D6, R4.Pin_1
  N6: Bauteil1.D7, R2.Pin_1
  N7: Bauteil1.D8, R3.Pin_1
  N8: Bauteil1.D11/MOSI, IC1.STROBE
  +5V: Bauteil1.5V, NEOPIXEL1.+5V, NEOPIXEL2.+5V, NEOPIXEL3.+5V, NEOPIXEL4.+5V, NEOPIXEL5.+5V, NEOPIXEL6.+5V, NEOPIXEL7.+5V, IC1.VDD, R10.Pin_1, C4.0
  N9: Bauteil1.A1, IC1.DCOUT
  N10: NEOPIXEL1.DI, R1.Pin_0
  GND_2: NEOPIXEL1.GND#4, NEOPIXEL2.GND, NEOPIXEL3.GND, NEOPIXEL4.GND, NEOPIXEL5.GND, NEOPIXEL6.GND, NEOPIXEL7.GND#4
  N11: NEOPIXEL2.DI, R7.Pin_0
  N12: NEOPIXEL3.DI, R6.Pin_0
  N13: NEOPIXEL4.DI, R5.Pin_0
  N14: NEOPIXEL5.DI, R4.Pin_0
  N15: NEOPIXEL6.DI, R2.Pin_0
  N16: NEOPIXEL7.DI, R3.Pin_0
  N17: IC1.AUDIO_IN, C1.1
  N18: IC1.CG, C3.1
  N19: IC1.CKIN, R10.Pin_0, C2.1
  N20: U1.RIGHT, R8.Pin_0
  N21: U1.SLEEVE, R9.Pin_0
  N22: R8.Pin_1, R9.Pin_1, C1.0

notes:
  10 LEDs each
  7x 220R
  to External 5V Power Supply

custom parts:
  Neopixel Strip -- White (60/m): Neopixel Strip, White, 60 pixels per meter.
